// Logisim project Project2_pipelined.circ as structural Verilog: 9 circuits, main circuit Forwarding Unit
// Registers
module main (
  input  [2:0] RW,
  input  CLK,
  input  [15:0] Write_Register_Data,
  input  Register_Write,
  input  [2:0] RA,
  input  [2:0] RB,
  output [15:0] BUS_A,
  output [15:0] BUS_B
);

  wire and_1_out, and_2_out, and_3_out, and_4_out, and_5_out, and_6_out, and_7_out, and_8_out,
       decoder_1_out0, decoder_1_out1, decoder_1_out2, decoder_1_out3, decoder_1_out4, decoder_1_out5,
       decoder_1_out6, decoder_1_out7, undriven, undriven_2, undriven_3, undriven_4, undriven_5, undriven_6,
       undriven_7;
  wire [15:0] register_1_q, register_2_q, register_3_q, register_4_q, register_5_q, register_6_q,
       register_7_q, register_8_q;

  Decoder #(.select(3), .enable("false")) decoder_1 (
    .out0(decoder_1_out0), .out1(decoder_1_out1), .out2(decoder_1_out2), .out3(decoder_1_out3),
    .out4(decoder_1_out4), .out5(decoder_1_out5), .out6(decoder_1_out6), .out7(decoder_1_out7), .sel(RW));
  and and_1 (and_1_out, decoder_1_out0, Register_Write);
  and and_2 (and_2_out, decoder_1_out1, Register_Write);
  and and_3 (and_3_out, decoder_1_out2, Register_Write);
  and and_4 (and_4_out, decoder_1_out3, Register_Write);
  and and_5 (and_5_out, decoder_1_out4, Register_Write);
  and and_6 (and_6_out, decoder_1_out5, Register_Write);
  and and_7 (and_7_out, decoder_1_out6, Register_Write);
  and and_8 (and_8_out, decoder_1_out7, Register_Write);
  Register #(.width(16), .trigger("falling")) register_1 (
    .D(Write_Register_Data), .en(and_1_out), .Q(register_1_q), .clk(CLK), .clr(1'b1));
  Register #(.width(16), .trigger("falling")) register_2 (
    .D(Write_Register_Data), .en(and_2_out), .Q(register_2_q), .clk(CLK), .clr(undriven));
  Register #(.width(16), .trigger("falling")) register_3 (
    .D(Write_Register_Data), .en(and_3_out), .Q(register_3_q), .clk(CLK), .clr(undriven_2));
  Register #(.width(16), .trigger("falling")) register_4 (
    .D(Write_Register_Data), .en(and_4_out), .Q(register_4_q), .clk(CLK), .clr(undriven_3));
  Register #(.width(16), .trigger("falling")) register_5 (
    .D(Write_Register_Data), .en(and_5_out), .Q(register_5_q), .clk(CLK), .clr(undriven_4));
  Register #(.width(16), .trigger("falling")) register_6 (
    .D(Write_Register_Data), .en(and_6_out), .Q(register_6_q), .clk(CLK), .clr(undriven_5));
  Register #(.width(16), .trigger("falling")) register_7 (
    .D(Write_Register_Data), .en(and_7_out), .Q(register_7_q), .clk(CLK), .clr(undriven_6));
  Register #(.width(16), .trigger("falling")) register_8 (
    .D(Write_Register_Data), .en(and_8_out), .Q(register_8_q), .clk(CLK), .clr(undriven_7));
  Multiplexer #(.select(3), .width(16), .enable("false")) multiplexer_1 (
    .in0(register_1_q), .in1(register_2_q), .in2(register_3_q), .in3(register_4_q), .in4(register_5_q),
    .in5(register_6_q), .in6(register_7_q), .in7(register_8_q), .out(BUS_A), .sel(RA));
  Multiplexer #(.select(3), .width(16), .enable("false")) multiplexer_2 (
    .in0(register_1_q), .in1(register_2_q), .in2(register_3_q), .in3(register_4_q), .in4(register_5_q),
    .in5(register_6_q), .in6(register_7_q), .in7(register_8_q), .out(BUS_B), .sel(RB));
endmodule

// Register File
module Register_File_Component (
  input  [2:0] RA,
  input  [2:0] RB,
  input  [2:0] RW,
  input  [15:0] Register_Write_Data,
  input  Register_Write_Enable,
  input  CLK,
  output [15:0] BUS_A,
  output [15:0] BUS_B
);

  main main_1 ();  // open: RW, Write_Register_Data, Register_Write, RA, RB, CLK, BUS_A, BUS_B

  assign BUS_B = BUS_A;
endmodule

module ALU (
  input  [15:0] ALUInput1,
  input  [15:0] ALUInput2,
  input  [2:0] ALUOperation,
  output zero,
  output [15:0] ALUResult
);

  wire comparator_1_gt, comparator_1_lt;
  wire [15:0] adder_1_out, and_1_out, multiplexer_1_out, multiplexer_2_out, or_1_out, shifter_1_out,
       subtractor_1_out;

  Adder #(.width(16)) adder_1 (.a(ALUInput1), .b(ALUInput2), .out(adder_1_out), .cin(1'b0));  // open: cout
  Subtractor #(.width(16)) subtractor_1 (
    .a(ALUInput1), .b(ALUInput2), .out(subtractor_1_out), .bin(1'b0));  // open: bout
  Comparator #(.width(16)) comparator_1 (
    .a(ALUInput1), .b(ALUInput2), .gt(comparator_1_gt), .eq(zero), .lt(comparator_1_lt));
  Shifter #(.width(16)) shifter_1 (.in(ALUInput2), .\dist (4'b0100), .out(shifter_1_out));
  assign and_1_out = ALUInput1 & ALUInput2;  // AND_Gate and_1, 16 bits wide
  assign or_1_out = ALUInput1 | ALUInput2;  // OR_Gate or_1, 16 bits wide
  Multiplexer #(.width(16), .enable("false")) multiplexer_1 (
    .in0(ALUInput2), .in1(ALUInput1), .out(multiplexer_1_out), .sel(comparator_1_gt));
  Multiplexer #(.width(16), .enable("false")) multiplexer_2 (
    .in0({16{1'b0}}), .in1(16'h1), .out(multiplexer_2_out), .sel(comparator_1_lt));
  Multiplexer #(.select(3), .width(16), .enable("false")) multiplexer_3 (
    .in0(adder_1_out), .in1(subtractor_1_out), .in2(multiplexer_2_out), .in3(and_1_out), .in4(or_1_out),
    .in5(shifter_1_out), .in6(multiplexer_1_out), .out(ALUResult), .sel(ALUOperation));  // open: in7
endmodule

module Data_Path (
);

  wire clock_1_out, comparator_1_eq, cu_1_beq, cu_1_j, cu_1_jal, cu_1_jr, cu_1_load, cu_1_r_type, EX_MEM_5_q,
       hazard_detection_unit_1_stall_id_ex, hazard_detection_unit_1_stall_jump, ID_EX_6_q, ID_EX_7_q,
       nextpc_1_pc_src, not_1_out;
  wire [1:0] cu_1_destinationreg, cu_1_nextpc, cu_1_writeback, forwarding_unit_1_beq_forward_rt,
       forwarding_unit_1_forward_a, forwarding_unit_1_forward_b, forwarding_unit_1_jr_beq_forward_rs;
  wire [2:0] cu_1_alucontrol, EX_MEM_3_q, MEM_WB_4_q, multiplexer_4_out;
  wire [3:0] IF_ID_q_3;
  wire [4:0] MEM_WB_2_q;
  wire [5:0] cu_1_memwrite, IF_ID_q_2;
  wire [6:0] EX_MEM_q;
  wire [7:0] multiplexer_18_out;
  wire [8:0] ID_EX_4_q, multiplexer_10_out;
  wire [10:0] ID_EX_5_q, multiplexer_11_out;
  wire [11:6] IF_ID_q_4;
  wire [15:0] adder_1_out, alu_1_aluresult, bit_extender_1_out, bit_extender_2_out, EX_MEM_2_q_2, EX_MEM_4_q,
       extender_1_extendedout, ID_EX_2_q, ID_EX_3_q, IF_ID_2_q, IF_ID_q, main_1_bus_a, main_1_bus_b,
       MEM_WB_q, multiplexer_1_out, multiplexer_2_out, multiplexer_5_out, multiplexer_6_out,
       multiplexer_7_out, multiplexer_9_out, multiplexer_12_out, multiplexer_13_out, multiplexer_14_out,
       multiplexer_15_out, multiplexer_16_out, multiplexer_17_out, nextpc_1_target_address, PC_q, ram_1_data,
       ram_2_data;
  wire [15:8] multiplexer_18_out_2;
  wire [31:0] ID_EX_q, MEM_WB_3_q, multiplexer_3_out, multiplexer_8_out;
  wire [31:16] EX_MEM_2_q;

  Multiplexer #(.width(16), .enable("false")) multiplexer_1 (
    .in0(adder_1_out), .in1(nextpc_1_target_address), .out(multiplexer_1_out), .sel(nextpc_1_pc_src));
  not not_1 (not_1_out, hazard_detection_unit_1_stall_id_ex);
  Register #(.width(16)) PC (.D(multiplexer_1_out), .en(not_1_out), .Q(PC_q), .clk(clock_1_out));  // open: clr
  Adder #(.width(16)) adder_1 (.a(16'h1), .b(PC_q), .out(adder_1_out), .cin(1'b0));  // open: cout
  RAM #(.addrWidth(16), .dataWidth(16)) ram_1 (
    .addr(PC_q), .data(ram_1_data), .sel(1'b1), .clk(clock_1_out), .ld(1'b1), .clr(1'b0));
  Multiplexer #(.width(16), .enable("false")) multiplexer_2 (
    .in0(adder_1_out), .in1(16'h1000), .out(multiplexer_2_out), .sel(hazard_detection_unit_1_stall_jump));
  Hazard_Detection_Unit hazard_detection_unit_1 (
    .ID___EX_MemRead(ID_EX_5_q[1]), .ID___EX_Rt(ID_EX_4_q[5:3]), .IF___ID_Rs(IF_ID_q_4[11:9]),
    .IF___ID_Rt(IF_ID_q_4[8:6]), .Stall_ID_EX(hazard_detection_unit_1_stall_id_ex), .EX_MEM_Rt(EX_MEM_3_q),
    .JR(cu_1_jr), .Beq(cu_1_beq), .AnyJump(nextpc_1_pc_src), .Stall_Jump(hazard_detection_unit_1_stall_jump),
    .EX_MEM_Load(EX_MEM_5_q));
  Register #(.width(32)) IF_ID (
    .D(multiplexer_3_out), .en(not_1_out), .Q({IF_ID_q_3, IF_ID_q_4, IF_ID_q_2, IF_ID_q}), .clk(clock_1_out));  // open: clr
  Multiplexer #(.width(32), .enable("false")) multiplexer_3 (
    .in0({ram_1_data, adder_1_out}), .in1(32'h10001000), .out(multiplexer_3_out),
    .sel(hazard_detection_unit_1_stall_jump));
  Register #(.width(16)) IF_ID_2 (
    .D(multiplexer_2_out), .en(not_1_out), .Q(IF_ID_2_q), .clk(clock_1_out));  // open: clr
  assign bit_extender_1_out = {{10{IF_ID_q_2[5]}}, IF_ID_q_2};  // Bit_Extender bit_extender_1
  Multiplexer #(.select(2), .width(3), .enable("false")) multiplexer_4 (
    .in0(IF_ID_q_4[8:6]), .in1(IF_ID_q_2[5:3]), .in2(3'b111), .in3(3'b001), .out(multiplexer_4_out),
    .sel(cu_1_destinationreg));
  CU cu_1 (
    .funct(IF_ID_q_2[2:0]), .OP(IF_ID_q_3), .JR(cu_1_jr), .ALUControl(cu_1_alucontrol),
    .RegWrite(cu_1_memwrite[5]), .ALUSource(cu_1_memwrite[4]), .BEQ(cu_1_beq), .J(cu_1_j),
    .MemRead(cu_1_memwrite[1]), .MemWrite(cu_1_memwrite[0]), .ExtendedStore(cu_1_memwrite[2]),
    .ExtendLoadByte(cu_1_memwrite[3]), .JAL(cu_1_jal), .DestinationReg(cu_1_destinationreg),
    .NextPC(cu_1_nextpc), .WriteBack(cu_1_writeback), .Load(cu_1_load), .R_Type(cu_1_r_type));
  NextPc nextpc_1 (
    .PC(IF_ID_q), ._12_bit_Immediate({IF_ID_q_4, IF_ID_q_2}), .Jump_OR_BEQ_OR_JR(cu_1_nextpc),
    .RS(multiplexer_5_out), .Zero_Flag(comparator_1_eq), .BEQ(cu_1_beq), .J(cu_1_j), .JR(cu_1_jr),
    .JAL(cu_1_jal), .Target_Address(nextpc_1_target_address), .PC_Src(nextpc_1_pc_src));
  main main_1 (
    .RW(MEM_WB_4_q), .Write_Register_Data(multiplexer_15_out), .Register_Write(MEM_WB_2_q[2]),
    .RA(IF_ID_q_4[11:9]), .RB(IF_ID_q_4[8:6]), .CLK(clock_1_out), .BUS_A(main_1_bus_a), .BUS_B(main_1_bus_b));
  Clock clock_1 (.out(clock_1_out));
  Multiplexer #(.select(2), .width(16), .enable("false")) multiplexer_5 (
    .in0(main_1_bus_a), .in1(alu_1_aluresult), .in2(EX_MEM_2_q_2), .out(multiplexer_5_out),
    .sel(forwarding_unit_1_jr_beq_forward_rs));  // open: in3
  Multiplexer #(.select(2), .width(16), .enable("false")) multiplexer_6 (
    .in0(main_1_bus_b), .in1(alu_1_aluresult), .in2(EX_MEM_2_q_2), .out(multiplexer_6_out),
    .sel(forwarding_unit_1_beq_forward_rt));  // open: in3
  Comparator #(.width(16)) comparator_1 (
    .a(multiplexer_5_out), .b(multiplexer_6_out), .eq(comparator_1_eq));  // open: gt, lt
  Multiplexer #(.width(16), .enable("false")) multiplexer_7 (
    .in0(IF_ID_2_q), .in1({16{1'b0}}), .out(multiplexer_7_out), .sel(hazard_detection_unit_1_stall_id_ex));
  Register #(.width(32)) ID_EX (.D(multiplexer_8_out), .Q(ID_EX_q), .clk(clock_1_out));  // open: en, clr
  Multiplexer #(.width(32), .enable("false")) multiplexer_8 (
    .in0({main_1_bus_b, main_1_bus_a}), .in1({32{1'b0}}), .out(multiplexer_8_out),
    .sel(hazard_detection_unit_1_stall_id_ex));
  Multiplexer #(.width(16), .enable("false")) multiplexer_9 (
    .in0(bit_extender_1_out), .in1({16{1'b0}}), .out(multiplexer_9_out),
    .sel(hazard_detection_unit_1_stall_id_ex));
  Multiplexer #(.width(9), .enable("false")) multiplexer_10 (
    .in0({multiplexer_4_out, IF_ID_q_4[8:6], IF_ID_q_4[11:9]}), .in1({9{1'b0}}), .out(multiplexer_10_out),
    .sel(hazard_detection_unit_1_stall_id_ex));
  Register #(.width(16)) ID_EX_2 (.D(multiplexer_7_out), .Q(ID_EX_2_q), .clk(clock_1_out));  // open: en, clr
  Multiplexer #(.width(11), .enable("false")) multiplexer_11 (
    .in0({cu_1_alucontrol, cu_1_writeback, cu_1_memwrite}), .in1({11{1'b0}}), .out(multiplexer_11_out),
    .sel(hazard_detection_unit_1_stall_id_ex));
  Register #(.width(16)) ID_EX_3 (.D(multiplexer_9_out), .Q(ID_EX_3_q), .clk(clock_1_out));  // open: en, clr
  Register #(.width(9)) ID_EX_4 (.D(multiplexer_10_out), .Q(ID_EX_4_q), .clk(clock_1_out));  // open: en, clr
  Register #(.width(11)) ID_EX_5 (.D(multiplexer_11_out), .Q(ID_EX_5_q), .clk(clock_1_out));  // open: en, clr
  Multiplexer #(.select(2), .width(16), .enable("false")) multiplexer_12 (
    .in0(ID_EX_q[15:0]), .in1(multiplexer_15_out), .in2(EX_MEM_2_q_2), .out(multiplexer_12_out),
    .sel(forwarding_unit_1_forward_a));  // open: in3
  Multiplexer #(.width(16), .enable("false")) multiplexer_13 (
    .in0(multiplexer_14_out), .in1(ID_EX_3_q), .out(multiplexer_13_out), .sel(ID_EX_5_q[4]));
  Multiplexer #(.select(2), .width(16), .enable("false")) multiplexer_14 (
    .in0(ID_EX_q[31:16]), .in1(multiplexer_15_out), .in2(EX_MEM_2_q_2), .out(multiplexer_14_out),
    .sel(forwarding_unit_1_forward_b));  // open: in3
  Register #(.width(1)) ID_EX_6 (.D(cu_1_load), .Q(ID_EX_6_q), .clk(clock_1_out));  // open: en, clr
  Register #(.width(1)) ID_EX_7 (.D(cu_1_r_type), .Q(ID_EX_7_q), .clk(clock_1_out));  // open: en, clr
  ALU alu_1 (
    .ALUInput1(multiplexer_12_out), .ALUInput2(multiplexer_13_out), .ALUResult(alu_1_aluresult),
    .ALUOperation(ID_EX_5_q[10:8]));  // open: zero
  Forwarding_Unit forwarding_unit_1 (
    .EX___MEM_RegWrite(EX_MEM_q[4]), .EX___MEM_Rd(EX_MEM_3_q), .ID___EX_Rs(ID_EX_4_q[2:0]),
    .MEM___WB_RegWrite(MEM_WB_2_q[2]), .ID___EX_Rt(ID_EX_4_q[5:3]), .MEM___WB_Rd(MEM_WB_4_q),
    .Forward_A(forwarding_unit_1_forward_a), .Forward_B(forwarding_unit_1_forward_b),
    .ID_EX_RegW(ID_EX_5_q[5]), .ID_EX_Rd(ID_EX_4_q[8:6]), .IF_ID_Rs(IF_ID_q_4[11:9]),
    .JR_BEQ_Forward_Rs(forwarding_unit_1_jr_beq_forward_rs),
    .BEQ_Forward_Rt(forwarding_unit_1_beq_forward_rt), .IF_ID_Rt(IF_ID_q_4[8:6]));
  Register #(.width(7)) EX_MEM (
    .D({ID_EX_5_q[7:5], ID_EX_5_q[3:0]}), .Q(EX_MEM_q), .clk(clock_1_out));  // open: en, clr
  Register #(.width(32)) EX_MEM_2 (
    .D({multiplexer_14_out, alu_1_aluresult}), .Q({EX_MEM_2_q, EX_MEM_2_q_2}), .clk(clock_1_out));  // open: en, clr
  Register #(.width(3)) EX_MEM_3 (.D(ID_EX_4_q[8:6]), .Q(EX_MEM_3_q), .clk(clock_1_out));  // open: en, clr
  Register #(.width(16)) EX_MEM_4 (.D(ID_EX_2_q), .Q(EX_MEM_4_q), .clk(clock_1_out));  // open: en, clr
  Register #(.width(1)) EX_MEM_5 (.D(ID_EX_6_q), .Q(EX_MEM_5_q), .clk(clock_1_out));  // open: en, clr
  assign bit_extender_2_out = {{8{1'b0}}, EX_MEM_2_q[23:16]};  // Bit_Extender bit_extender_2
  Multiplexer #(.select(2), .width(16), .enable("false")) multiplexer_15 (
    .in0({multiplexer_18_out_2, multiplexer_18_out}), .in1(extender_1_extendedout), .in2(MEM_WB_q),
    .out(multiplexer_15_out), .sel(MEM_WB_2_q[4:3]));  // open: in3
  Multiplexer #(.width(16), .enable("false")) multiplexer_16 (
    .in0(EX_MEM_2_q), .in1(bit_extender_2_out), .out(multiplexer_16_out), .sel(EX_MEM_q[2]));
  Register #(.width(16)) MEM_WB (.D(EX_MEM_4_q), .Q(MEM_WB_q), .clk(clock_1_out));  // open: en, clr
  RAM #(.addrWidth(16), .dataWidth(16), .bus("separate")) ram_2 (
    .addr(EX_MEM_2_q_2), .din(multiplexer_16_out), .data(ram_2_data), .str(EX_MEM_q[0]), .clk(clock_1_out),
    .ld(EX_MEM_q[1]));  // open: sel, clr
  Extender extender_1 (.ExtenderOP(MEM_WB_2_q[1]), .Input(multiplexer_18_out), .ExtendedOut(extender_1_extendedout));
  Multiplexer #(.width(16), .enable("false")) multiplexer_17 (
    .in0({16{1'b0}}), .in1(ram_2_data), .out(multiplexer_17_out), .sel(EX_MEM_q[1]));
  Register #(.width(5)) MEM_WB_2 (
    .D({EX_MEM_q[6:3], EX_MEM_q[1]}), .Q(MEM_WB_2_q), .clk(clock_1_out));  // open: en, clr
  Register #(.width(32)) MEM_WB_3 (
    .D({multiplexer_17_out, EX_MEM_2_q_2}), .Q(MEM_WB_3_q), .clk(clock_1_out));  // open: en, clr
  Register #(.width(3)) MEM_WB_4 (.D(EX_MEM_3_q), .Q(MEM_WB_4_q), .clk(clock_1_out));  // open: en, clr
  Multiplexer #(.width(16), .enable("false")) multiplexer_18 (
    .in0(MEM_WB_3_q[15:0]), .in1(MEM_WB_3_q[31:16]), .out({multiplexer_18_out_2, multiplexer_18_out}),
    .sel(MEM_WB_2_q[0]));
endmodule

module Extender (
  input  ExtenderOP,
  input  [7:0] Input,
  output [15:0] ExtendedOut
);

  and and_1 (ExtendedOut[15], ExtenderOP, Input[7]);

  assign ExtendedOut[14:0] = {{7{ExtendedOut[15]}}, Input};
endmodule

// Next PC
module NextPc (
  input  [15:0] PC,
  input  [11:0] _12_bit_Immediate,
  input  [1:0] Jump_OR_BEQ_OR_JR,
  input  [15:0] RS,
  input  Zero_Flag,
  input  BEQ,
  input  J,
  input  JR,
  input  JAL,
  output [15:0] Target_Address,
  output PC_Src
);

  wire and_1_out;
  wire [15:0] adder_1_out, adder_2_out, bit_extender_1_out, bit_extender_2_out;

  assign bit_extender_1_out = {{4{1'b0}}, _12_bit_Immediate};  // Bit_Extender bit_extender_1
  assign bit_extender_2_out = {{10{_12_bit_Immediate[5]}}, _12_bit_Immediate[5:0]};  // Bit_Extender bit_extender_2
  and and_1 (and_1_out, Zero_Flag, BEQ);
  Adder #(.width(16)) adder_1 (.a(PC), .b(bit_extender_1_out), .out(adder_1_out), .cin(1'b0));  // open: cout
  Adder #(.width(16)) adder_2 (.a(PC), .b(bit_extender_2_out), .out(adder_2_out), .cin(1'b0));  // open: cout
  Multiplexer #(.select(2), .width(16), .enable("false")) multiplexer_1 (
    .in0(adder_2_out), .in1(adder_1_out), .in2(RS), .out(Target_Address), .sel(Jump_OR_BEQ_OR_JR));  // open: in3
  or or_1 (PC_Src, and_1_out, J, JR, JAL);
endmodule

// Control Unit
module CU (
  input  [2:0] funct,
  input  [3:0] OP,
  output JR,
  output [2:0] ALUControl,
  output RegWrite,
  output ALUSource,
  output BEQ,
  output J,
  output MemRead,
  output MemWrite,
  output ExtendedStore,
  output ExtendLoadByte,
  output JAL,
  output [1:0] DestinationReg,
  output [1:0] NextPC,
  output [1:0] WriteBack,
  output Load,
  output R_Type
);

  wire and_2_out, and_3_out, and_4_out, and_5_out, and_6_out, and_7_out, decoder_1_out0, decoder_1_out1,
       decoder_1_out2, decoder_1_out4, decoder_1_out5, decoder_1_out6, decoder_1_out7, decoder_2_out1,
       decoder_2_out2, decoder_2_out4, decoder_2_out5, decoder_2_out7, decoder_2_out12;

  Decoder #(.select(3), .enable("false")) decoder_1 (
    .out0(decoder_1_out0), .out1(decoder_1_out1), .out2(decoder_1_out2), .out4(decoder_1_out4),
    .out5(decoder_1_out5), .out6(decoder_1_out6), .out7(decoder_1_out7), .sel(funct));  // open: out3
  Decoder #(.select(4), .enable("false")) decoder_2 (
    .out0(R_Type), .out1(decoder_2_out1), .out2(decoder_2_out2), .out4(decoder_2_out4),
    .out5(decoder_2_out5), .out6(ExtendLoadByte), .out7(decoder_2_out7), .out8(ExtendedStore), .out9(BEQ),
    .out10(J), .out11(JAL), .out12(decoder_2_out12), .sel(OP));  // open: out3, out13, out14, out15
  and and_1 (JR, R_Type, decoder_1_out0);
  and and_2 (and_2_out, R_Type, decoder_1_out4);
  and and_3 (and_3_out, R_Type, decoder_1_out1);
  or or_1 (NextPC[0], J, JAL);
  or or_2 (WriteBack[0], decoder_2_out5, ExtendLoadByte);
  and and_4 (and_4_out, R_Type, decoder_1_out2);
  or or_3 (DestinationReg[1], JAL, decoder_2_out12);
  or or_4 (DestinationReg[0], R_Type, decoder_2_out12);
  and and_5 (and_5_out, R_Type, decoder_1_out5);
  and and_6 (and_6_out, R_Type, decoder_1_out6);
  nor nor_1 (RegWrite, JR, decoder_2_out7, ExtendedStore, BEQ, J);
  nor nor_2 (ALUSource, R_Type, BEQ);
  or or_5 (MemRead, and_2_out, decoder_2_out4, decoder_2_out5, ExtendLoadByte);
  or or_6 (MemWrite, decoder_2_out7, ExtendedStore);
  and and_7 (and_7_out, R_Type, decoder_1_out7);
  or or_7 (Load, ExtendLoadByte, decoder_2_out5, decoder_2_out4);
  or or_8 (ALUControl[2], and_5_out, and_6_out, decoder_2_out2, decoder_2_out12);
  or or_9 (ALUControl[1], and_7_out, and_5_out, and_3_out, decoder_2_out1);
  or or_10 (ALUControl[0], and_4_out, and_7_out, decoder_2_out1, BEQ, decoder_2_out12);

  assign NextPC[1] = JR;
  assign WriteBack[1] = JAL;
endmodule

// Forwarding
module Forwarding_Unit (
  input  EX___MEM_RegWrite,
  input  [2:0] EX___MEM_Rd,
  input  [2:0] ID___EX_Rs,
  input  MEM___WB_RegWrite,
  input  [2:0] ID___EX_Rt,
  input  [2:0] MEM___WB_Rd,
  input  ID_EX_RegW,
  input  [2:0] ID_EX_Rd,
  input  [2:0] IF_ID_Rs,
  input  [2:0] IF_ID_Rt,
  output [1:0] Forward_A,
  output [1:0] Forward_B,
  output [1:0] JR_BEQ_Forward_Rs,
  output [1:0] BEQ_Forward_Rt
);

  wire comparator_1_eq, comparator_2_eq, comparator_3_eq, comparator_4_eq, comparator_5_eq, comparator_6_eq,
       comparator_7_eq, comparator_8_eq, comparator_9_eq, comparator_10_eq, comparator_11_eq,
       comparator_12_eq, comparator_13_eq, comparator_14_eq, comparator_15_eq, comparator_16_eq,
       comparator_17_eq, comparator_18_eq, comparator_19_eq, comparator_20_eq, not_1_out, not_2_out,
       not_3_out, not_4_out, not_5_out, not_6_out, not_7_out, not_8_out, not_9_out, not_10_out, not_11_out,
       not_12_out;

  Comparator #(.width(3)) comparator_1 (.a(EX___MEM_Rd), .b(3'b000), .eq(comparator_1_eq));  // open: gt, lt
  Comparator #(.width(3)) comparator_2 (.a(EX___MEM_Rd), .b(ID___EX_Rs), .eq(comparator_2_eq));  // open: gt, lt
  Comparator #(.width(3)) comparator_3 (.a(ID_EX_Rd), .b(3'b000), .eq(comparator_3_eq));  // open: gt, lt
  Comparator #(.width(3)) comparator_4 (.a(ID_EX_Rd), .b(IF_ID_Rs), .eq(comparator_4_eq));  // open: gt, lt
  Comparator #(.width(3)) comparator_5 (.a(EX___MEM_Rd), .b(3'b000), .eq(comparator_5_eq));  // open: gt, lt
  Comparator #(.width(3)) comparator_6 (.a(EX___MEM_Rd), .b(IF_ID_Rs), .eq(comparator_6_eq));  // open: gt, lt
  Comparator #(.width(3)) comparator_7 (.a(ID_EX_Rd), .b(EX___MEM_Rd), .eq(comparator_7_eq));  // open: gt, lt
  not not_1 (not_1_out, comparator_1_eq);
  not not_2 (not_2_out, comparator_8_eq);
  Comparator #(.width(3)) comparator_8 (.a(MEM___WB_Rd), .b(3'b000), .eq(comparator_8_eq));  // open: gt, lt
  Comparator #(.width(3)) comparator_9 (.a(EX___MEM_Rd), .b(ID___EX_Rs), .eq(comparator_9_eq));  // open: gt, lt
  not not_3 (not_3_out, comparator_9_eq);
  Comparator #(.width(3)) comparator_10 (.a(MEM___WB_Rd), .b(ID___EX_Rs), .eq(comparator_10_eq));  // open: gt, lt
  not not_4 (not_4_out, comparator_3_eq);
  not not_5 (not_5_out, comparator_5_eq);
  not not_6 (not_6_out, comparator_7_eq);
  and and_1 (JR_BEQ_Forward_Rs[0], ID_EX_RegW, not_4_out, comparator_4_eq);
  and and_2 (JR_BEQ_Forward_Rs[1], EX___MEM_RegWrite, not_5_out, comparator_6_eq, not_6_out);
  and and_3 (Forward_A[1], EX___MEM_RegWrite, not_1_out, comparator_2_eq);
  and and_4 (Forward_A[0], MEM___WB_RegWrite, not_2_out, not_3_out, comparator_10_eq);
  Comparator #(.width(3)) comparator_11 (.a(EX___MEM_Rd), .b(3'b000), .eq(comparator_11_eq));  // open: gt, lt
  Comparator #(.width(3)) comparator_12 (.a(EX___MEM_Rd), .b(ID___EX_Rt), .eq(comparator_12_eq));  // open: gt, lt
  not not_7 (not_7_out, comparator_11_eq);
  Comparator #(.width(3)) comparator_13 (.a(MEM___WB_Rd), .b(3'b000), .eq(comparator_13_eq));  // open: gt, lt
  Comparator #(.width(3)) comparator_14 (.a(EX___MEM_Rd), .b(ID___EX_Rt), .eq(comparator_14_eq));  // open: gt, lt
  Comparator #(.width(3)) comparator_15 (.a(MEM___WB_Rd), .b(ID___EX_Rt), .eq(comparator_15_eq));  // open: gt, lt
  Comparator #(.width(3)) comparator_16 (.a(ID_EX_Rd), .b(3'b000), .eq(comparator_16_eq));  // open: gt, lt
  Comparator #(.width(3)) comparator_17 (.a(ID_EX_Rd), .b(IF_ID_Rt), .eq(comparator_17_eq));  // open: gt, lt
  Comparator #(.width(3)) comparator_18 (.a(EX___MEM_Rd), .b(3'b000), .eq(comparator_18_eq));  // open: gt, lt
  Comparator #(.width(3)) comparator_19 (.a(EX___MEM_Rd), .b(IF_ID_Rt), .eq(comparator_19_eq));  // open: gt, lt
  Comparator #(.width(3)) comparator_20 (.a(ID_EX_Rd), .b(EX___MEM_Rd), .eq(comparator_20_eq));  // open: gt, lt
  not not_8 (not_8_out, comparator_13_eq);
  not not_9 (not_9_out, comparator_14_eq);
  not not_10 (not_10_out, comparator_16_eq);
  not not_11 (not_11_out, comparator_18_eq);
  not not_12 (not_12_out, comparator_20_eq);
  and and_5 (Forward_B[1], EX___MEM_RegWrite, not_7_out, comparator_12_eq);
  and and_6 (Forward_B[0], MEM___WB_RegWrite, not_8_out, not_9_out, comparator_15_eq);
  and and_7 (BEQ_Forward_Rt[0], ID_EX_RegW, not_10_out, comparator_17_eq);
  and and_8 (BEQ_Forward_Rt[1], EX___MEM_RegWrite, not_11_out, comparator_19_eq, not_12_out);
endmodule

// Hazard Detection
module Hazard_Detection_Unit (
  input  ID___EX_MemRead,
  input  [2:0] ID___EX_Rt,
  input  [2:0] IF___ID_Rs,
  input  [2:0] IF___ID_Rt,
  input  [2:0] EX_MEM_Rt,
  input  EX_MEM_Load,
  input  JR,
  input  Beq,
  input  AnyJump,
  output Stall_ID_EX,
  output Stall_Jump
);

  wire and_1_out, and_2_out, and_3_out, comparator_1_eq, comparator_2_eq, comparator_3_eq, comparator_4_eq,
       comparator_5_eq, comparator_6_eq, not_1_out, not_2_out, or_1_out, or_2_out;

  Comparator #(.width(3)) comparator_1 (.a(ID___EX_Rt), .b(IF___ID_Rs), .eq(comparator_1_eq));  // open: gt, lt
  Comparator #(.width(3)) comparator_2 (.a(ID___EX_Rt), .b(IF___ID_Rt), .eq(comparator_2_eq));  // open: gt, lt
  Comparator #(.width(3)) comparator_3 (.a(EX_MEM_Rt), .b(IF___ID_Rt), .eq(comparator_3_eq));  // open: gt, lt
  Comparator #(.width(3)) comparator_4 (.a(ID___EX_Rt), .b(3'b000), .eq(comparator_4_eq));  // open: gt, lt
  Comparator #(.width(3)) comparator_5 (.a(EX_MEM_Rt), .b(3'b000), .eq(comparator_5_eq));  // open: gt, lt
  Comparator #(.width(3)) comparator_6 (.a(EX_MEM_Rt), .b(IF___ID_Rs), .eq(comparator_6_eq));  // open: gt, lt
  or or_1 (or_1_out, comparator_1_eq, comparator_2_eq);
  not not_1 (not_1_out, comparator_4_eq);
  not not_2 (not_2_out, comparator_5_eq);
  or or_2 (or_2_out, comparator_6_eq, comparator_3_eq);
  and and_1 (and_1_out, not_2_out, comparator_6_eq, JR, EX_MEM_Load);
  and and_2 (and_2_out, not_2_out, or_2_out, Beq, EX_MEM_Load);
  and and_3 (and_3_out, ID___EX_MemRead, or_1_out, not_1_out);
  or or_3 (Stall_ID_EX, and_3_out, and_1_out, and_2_out);

  assign Stall_Jump = AnyJump;
endmodule
